# Fritzing sketch Led_board_DEF (saved by Fritzing 0.9.3b)
perfboards: 1

parts:
  LED1 = Super Flux LED blue [color=Blue]
  LED3 = Super Flux LED blue [color=Green]
  LED5 = Super Flux LED blue [color=Orange]
  LED6 = Super Flux LED blue [color=Orange]
  LED7 = Super Flux LED blue [color=White]
  LED8 = Super Flux LED blue [color=Red]
  R1 = Resistor Mini [tolerance=±5% resistance=100 package=THT]  # not connected
  Q1 = NPN-Transistor [package="TO92 [THT]"]
  R2 = Resistor Mini [tolerance=±5% resistance=100 package=THT]
  LED11 = Super Flux LED blue [color=Blue]
  LED12 = Super Flux LED blue [color=Green]
  R3 = Resistor Mini [tolerance=±5% resistance=100 package=THT]
  R4 = Resistor Mini [tolerance=±5% resistance=100 package=THT]
  R5 = Resistor Mini [tolerance=±5% resistance=100 package=THT]  # not connected
  R6 = Resistor Mini [tolerance=±5% resistance=100 package=THT]
  R7 = Resistor Mini [tolerance=±5% resistance=100 package=THT]
  R8 = Resistor Mini [tolerance=±5% resistance=100 package=THT]
  R9 = Resistor Mini [tolerance=±5% resistance=100 package=THT]
  R10 = Resistor Mini [tolerance=±5% resistance=100 package=THT]  # not connected
  LED13 = Super Flux LED blue [color=White]
  LED10 = Super Flux LED blue [color=Red]
  Q2 = NPN-Transistor [package="TO92 [THT]"]
  Q3 = NPN-Transistor [package="TO92 [THT]"]
  Q4 = NPN-Transistor [package="TO92 [THT]"]
  R12 = Resistor Mini [tolerance=±5% resistance=1k package=THT]
  R13 = Resistor Mini [tolerance=±5% resistance=1k package=THT]
  R14 = Resistor Mini [tolerance=±5% resistance=1k package=THT]
  R15 = Resistor Mini [tolerance=±5% resistance=1k package=THT]
  R16 = Resistor Mini [tolerance=±5% resistance=1k package=THT]
  R17 = Resistor Mini [tolerance=±5% resistance=1k package=THT]
  R18 = Resistor Mini [tolerance=±5% resistance=1k package=THT]
  R19 = Resistor Mini [tolerance=±5% resistance=1k package=THT]
  R20 = Resistor Mini [tolerance=±5% resistance=1k package=THT]
  R21 = Resistor Mini [tolerance=±5% resistance=1k package=THT]
  C1 = Electrolytic Capacitor [capacitance=1µF package="100 mil [THT, electrolytic]"]
  Part3 = Adafruit MAX4466 Electret Microphone Amplifier [part_number="Adafruit #1063"]
  Q6 = NPN-Transistor [package="TO92 [THT]"]
  Q7 = NPN-Transistor [package="TO92 [THT]"]
  Q8 = NPN-Transistor [package="TO92 [THT]"]
  Q9 = NPN-Transistor [package="TO92 [THT]"]
  Q10 = NPN-Transistor [package="TO92 [THT]"]
  Q11 = NPN-Transistor [package="TO92 [THT]"]
  Part4 = MAX32620FTHR

nets:
  N1: LED1.cathode, R3.Pin_1, Q8.E
  N2: LED3.anode, R8.Pin_1
  N3: LED3.cathode, R21.Pin_0, Part4.AIN1, Part4.SS
  N4: LED5.anode, R19.Pin_0, Q6.E, Part4.AIN3, Part4.CTS
  N5: LED6.cathode, Part3.OUT, Part4.AIN0
  N6: LED7.cathode, Q3.E
  N7: LED8.cathode, R9.Pin_1
  N8: Q1.B, R13.Pin_1
  N9: Q1.C, R2.Pin_1, LED11.anode, Q2.C, Q3.C, Q4.C, Q6.C, Q7.C, Q8.C, Q9.C, Q10.C, Q11.C, Part4.GND#45
  N10: R2.Pin_0, R3.Pin_0, R9.Pin_0, C1.+, Part3.VCC, Part4.SYS
  N11: LED11.cathode, R18.Pin_0, Part4.SCK
  N12: LED12.cathode, Q9.E
  N13: R4.Pin_0, R15.Pin_0, Part4.MISO
  N14: R6.Pin_0, LED13.cathode, Q10.E
  N15: R6.Pin_1, Part4.SRN
  N16: R7.Pin_1, R14.Pin_0, Part4.RX
  N17: LED10.anode, Q11.E
  N18: Q2.B, R17.Pin_1
  N19: Q3.B, R15.Pin_1
  N20: Q4.B, R18.Pin_1
  N21: R12.Pin_0, Part4.SCL1
  N22: R12.Pin_1, Q11.B
  N23: R13.Pin_0, Part4.TX
  N24: R14.Pin_1, Q6.B
  N25: R16.Pin_0, Part4.MOSI
  N26: R16.Pin_1, Q10.B
  N27: R17.Pin_0, Part4.SDA1
  N28: R19.Pin_1, Q9.B
  N29: R20.Pin_0, Part4.AIN2, Part4.RTS
  N30: R20.Pin_1, Q7.B
  N31: R21.Pin_1, Q8.B
  N32: C1.-, Part3.GND, Part4.GND#57

custom parts:
  Resistor Mini: A generic resistor (0.25W)
  Adafruit MAX4466 Electret Microphone Amplifier: Add an ear to your project with this well-designed electret microphone amplifier. This fully assembled and tested board comes with a 20-20KHz electret microphone soldered on. For the amplification, we use the Maxim MAX4466, an op-amp specifically designed for this delicate task! The amplifier has excellent power supply noise rejection, so this amplifier sounds really good and isn't nearly as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
  MAX32620FTHR: Custom Fritzing part created to support the Maxim Integrated evaluation board MAX32620FTHR
